// Logisim project trafficRacerVavassori.circ as structural Verilog: 13 circuits, main circuit main
module main (
);

  wire CLK, CLK_out, Dx, DxOk, Lose, Restart, Sx, SxOk, W;
  wire [2:0] Converter_to_3_c1, Converter_to_3_c2, Converter_to_3_c3, Converter_to_3_c4, Converter_to_3_c5,
       Converter_to_3_c6, Converter_to_3_c7;
  wire [3:0] mh, ml, sh, sl;
  wire [6:0] CR, LR, lr_controller_1_d;
  wire [15:0] Car_matrix_r1, Car_matrix_r2, Car_matrix_r3, Car_matrix_r4, Car_matrix_r5, Car_matrix_r6,
       Car_matrix_r7, gestore_schermo_1_c1o, gestore_schermo_1_c2o, gestore_schermo_1_c3o,
       gestore_schermo_1_c4o, gestore_schermo_1_c5o, gestore_schermo_1_c6o, gestore_schermo_1_c7o;

  Clock u_CLK (.out(CLK_out));
  Button u_Restart (.out(Restart));
  and and_1 (CLK, CLK_out, ~Lose, ~W);  // AND_Gate
  Illegal_moves illegal_moves_1 (.car_row(CR), .Sx(Sx), .Dx(Dx), .SxOk(SxOk), .DxOk(DxOk));
  car_matrix Car_matrix (
    .Clear(Restart), .CLK(CLK), .R1(Car_matrix_r1), .R2(Car_matrix_r2), .R3(Car_matrix_r3),
    .R4(Car_matrix_r4), .R5(Car_matrix_r5), .R6(Car_matrix_r6), .R7(Car_matrix_r7), .last_row__1(LR));
  gestore_schermo gestore_schermo_1 (
    .C1(Car_matrix_r1), .C2(Car_matrix_r2), .C3(Car_matrix_r3), .C4(Car_matrix_r4), .C5(Car_matrix_r5),
    .C6(Car_matrix_r6), .C7(Car_matrix_r7), .Lose(Lose), .Win(W), .C1o(gestore_schermo_1_c1o),
    .C2o(gestore_schermo_1_c2o), .C3o(gestore_schermo_1_c3o), .C4o(gestore_schermo_1_c4o),
    .C5o(gestore_schermo_1_c5o), .C6o(gestore_schermo_1_c6o), .C7o(gestore_schermo_1_c7o));
  Hex_Digit_Display hex_digit_display_1 (.value(mh));  // open: dp
  playercar playercar_1 (.Dx(DxOk), .Sx(SxOk), .Vittoria(W), .CLK(CLK), .Reset(Restart), .out_6(CR));
  Hex_Digit_Display hex_digit_display_2 (.value(ml));  // open: dp
  DotMatrix #(.matrixcols(7), .matrixrows(16)) dotmatrix_1 (
    .col0(gestore_schermo_1_c1o), .col1(gestore_schermo_1_c2o), .col2(gestore_schermo_1_c3o),
    .col3(gestore_schermo_1_c4o), .col4(gestore_schermo_1_c5o), .col5(gestore_schermo_1_c6o),
    .col6(gestore_schermo_1_c7o));
  DotMatrix #(.matrixcols(7), .matrixrows(1)) dotmatrix_2 (
    .col0(lr_controller_1_d[6]), .col1(lr_controller_1_d[5]), .col2(lr_controller_1_d[4]),
    .col3(lr_controller_1_d[3]), .col4(lr_controller_1_d[2]), .col5(lr_controller_1_d[1]),
    .col6(lr_controller_1_d[0]));
  DotMatrix #(.matrixcols(7), .matrixrows(3)) dotmatrix_3 (
    .col0(Converter_to_3_c7), .col1(Converter_to_3_c6), .col2(Converter_to_3_c5), .col3(Converter_to_3_c4),
    .col4(Converter_to_3_c3), .col5(Converter_to_3_c2), .col6(Converter_to_3_c1));
  _1_to_3_row_conv Converter_to_3 (
    .in_1(CR), .c1(Converter_to_3_c1), .c2(Converter_to_3_c2), .c3(Converter_to_3_c3),
    .c4(Converter_to_3_c4), .c5(Converter_to_3_c5), .c6(Converter_to_3_c6), .c7(Converter_to_3_c7));
  timer_with_reset timer_with_reset_1 (
    .Reset(Restart), .CLK(CLK), .MinHigh(mh), .MinLow(ml), .SecHigh(sh), .SecLow(sl), .Win(W));
  Hex_Digit_Display hex_digit_display_3 (.value(sl));  // open: dp
  Hex_Digit_Display hex_digit_display_4 (.value(sh));  // open: dp
  LR_controller lr_controller_1 (.LR(LR), .Win(W), .D(lr_controller_1_d));
  Button button_1 (.out(Sx));
  Button button_2 (.out(Dx));
  lose_check Lose_check (.Last_Row(LR), .Car_row(CR), .Lose(Lose));

  // Notes on the sheet:
  //   Per ricominciare la partita premere su reset
  //   Per spostarsi tenere premuto Sx o Dx (comandi)
  //   Mosse illegali
  //   Per iniziare abilitare la simulazione e i ticks del clock a 2Hz
  //   Controller timer
  //   Comandi
endmodule

module playercar (
  input  Dx,
  input  Sx,
  input  Vittoria,
  input  CLK,
  input  Reset,
  output [6:0] out_6
);

  wire and_2_out, NoMove, not_1_out;
  wire [1:0] multiplexer_1_out;
  wire [2:0] counter_1_q;
  wire [7:7] multiplexer_2_out;

  and and_1 (NoMove, ~Sx, ~Dx);  // AND_Gate
  and and_2 (and_2_out, ~NoMove, CLK);  // AND_Gate
  // Probe on multiplexer_1_out
  Multiplexer #(.select(2), .width(2)) multiplexer_1 (
    .in0(2'b10), .in1(2'b11), .in2(2'b01), .out(multiplexer_1_out), .sel({Sx, Dx}));  // open: in3, en
  Counter #(.width(3), .max('h6)) counter_1 (
    .load(multiplexer_1_out[1]), .D(counter_1_q), .count(multiplexer_1_out[0]), .Q(counter_1_q),
    .clk(and_2_out), .clr(Reset));  // open: carry
  Multiplexer #(.select(3), .width(8), .disabled(0)) multiplexer_2 (
    .in0(8'h8), .in1(8'h10), .in2(8'h20), .in3(8'h40), .in4(8'h1), .in5(8'h2), .in6(8'h4), .in7(8'h80),
    .out({multiplexer_2_out[7], out_6}), .sel(counter_1_q), .en(not_1_out));
  not not_1 (not_1_out, Vittoria);
  // also tied to GND on the sheet: multiplexer_2_out[7]

  // Notes on the sheet:
  //   1=00000001
  //   2=00000010
  //   4=00000100
  //   8=00001000
  //   10=00010000
  //   20=00100000
  //   40=01000000
  //   80=10000000
endmodule

module Col_mem (
  input  D,
  input  Clear,
  input  CLK,
  output [15:0] Output_Col,
  output last___1
);

  D_Flip_Flop d_ff_1 (.clk(CLK), .D(D), .Q(Output_Col[15]), .reset(Clear));  // open: Qn, preset, en
  D_Flip_Flop d_ff_2 (.clk(CLK), .D(Output_Col[15]), .Q(Output_Col[14]), .reset(Clear));  // open: Qn, preset, en
  D_Flip_Flop d_ff_3 (.clk(CLK), .D(Output_Col[14]), .Q(Output_Col[13]), .reset(Clear));  // open: Qn, preset, en
  D_Flip_Flop d_ff_4 (.clk(CLK), .D(Output_Col[13]), .Q(Output_Col[12]), .reset(Clear));  // open: Qn, preset, en
  D_Flip_Flop d_ff_5 (.clk(CLK), .D(Output_Col[12]), .Q(Output_Col[11]), .reset(Clear));  // open: Qn, preset, en
  D_Flip_Flop d_ff_6 (.clk(CLK), .D(Output_Col[11]), .Q(Output_Col[10]), .reset(Clear));  // open: Qn, preset, en
  D_Flip_Flop d_ff_7 (.clk(CLK), .D(Output_Col[10]), .Q(Output_Col[9]), .reset(Clear));  // open: Qn, preset, en
  D_Flip_Flop d_ff_8 (.clk(CLK), .D(Output_Col[9]), .Q(Output_Col[8]), .reset(Clear));  // open: Qn, preset, en
  D_Flip_Flop d_ff_9 (.clk(CLK), .D(Output_Col[8]), .Q(Output_Col[7]), .reset(Clear));  // open: Qn, preset, en
  D_Flip_Flop d_ff_10 (.clk(CLK), .D(Output_Col[7]), .Q(Output_Col[6]), .reset(Clear));  // open: Qn, preset, en
  D_Flip_Flop d_ff_11 (.clk(CLK), .D(Output_Col[6]), .Q(Output_Col[5]), .reset(Clear));  // open: Qn, preset, en
  D_Flip_Flop d_ff_12 (.clk(CLK), .D(Output_Col[5]), .Q(Output_Col[4]), .reset(Clear));  // open: Qn, preset, en
  D_Flip_Flop d_ff_13 (.clk(CLK), .D(Output_Col[4]), .Q(Output_Col[3]), .reset(Clear));  // open: Qn, preset, en
  D_Flip_Flop d_ff_14 (.clk(CLK), .D(Output_Col[3]), .Q(Output_Col[2]), .reset(Clear));  // open: Qn, preset, en
  D_Flip_Flop d_ff_15 (.clk(CLK), .D(Output_Col[2]), .Q(Output_Col[1]), .reset(Clear));  // open: Qn, preset, en
  D_Flip_Flop d_ff_16 (.clk(CLK), .D(Output_Col[1]), .Q(Output_Col[0]), .reset(Clear));  // open: Qn, preset, en
  D_Flip_Flop d_ff_17 (.clk(CLK), .D(Output_Col[0]), .Q(last___1), .reset(Clear));  // open: Qn, preset, en
endmodule

module car_matrix (
  input  Clear,
  input  CLK,
  output [15:0] R1,
  output [15:0] R2,
  output [15:0] R3,
  output [15:0] R4,
  output [15:0] R5,
  output [15:0] R6,
  output [15:0] R7,
  output [6:0] last_row__1
);

  wire and_1_out, decoder_1_out0, decoder_1_out1, decoder_1_out2, decoder_1_out3, decoder_1_out4,
       decoder_1_out5, decoder_1_out6, decoder_1_out7;
  wire [2:0] random_1_out;

  Col_mem col_mem_1 (.D(decoder_1_out0), .Clear(Clear), .CLK(CLK), .Output_Col(R1), .last___1(last_row__1[6]));
  Random #(.width(3)) random_1 (.clk(CLK), .out(random_1_out), .clr(and_1_out));  // open: next
  Col_mem col_mem_2 (.D(decoder_1_out1), .Clear(Clear), .CLK(CLK), .Output_Col(R2), .last___1(last_row__1[5]));
  Decoder #(.select(3), .enable("false")) decoder_1 (
    .out0(decoder_1_out0), .out1(decoder_1_out1), .out2(decoder_1_out2), .out3(decoder_1_out3),
    .out4(decoder_1_out4), .out5(decoder_1_out5), .out6(decoder_1_out6), .out7(decoder_1_out7),
    .sel(random_1_out));
  Col_mem col_mem_3 (.D(decoder_1_out2), .Clear(Clear), .CLK(CLK), .Output_Col(R3), .last___1(last_row__1[4]));
  and and_1 (and_1_out, random_1_out[0], random_1_out[1], random_1_out[2]);
  Col_mem col_mem_4 (.D(decoder_1_out3), .Clear(Clear), .CLK(CLK), .Output_Col(R4), .last___1(last_row__1[3]));
  Col_mem col_mem_5 (.D(decoder_1_out4), .Clear(Clear), .CLK(CLK), .Output_Col(R5), .last___1(last_row__1[2]));
  Col_mem col_mem_6 (.D(decoder_1_out5), .Clear(Clear), .CLK(CLK), .Output_Col(R6), .last___1(last_row__1[1]));
  Col_mem col_mem_7 (.D(decoder_1_out6), .Clear(Clear), .CLK(CLK), .Output_Col(R7), .last___1(last_row__1[0]));
  // also tied to GND on the sheet: decoder_1_out7

  // Other names for the same wires on the sheet: CL = Clear

  // Notes on the sheet:
  //   ricalcola se esce l'ottava
endmodule

module Illegal_moves (
  input  [6:0] car_row,
  input  Sx,
  input  Dx,
  output SxOk,
  output DxOk
);

  wire and_1_out, and_2_out, or_1_out;

  and and_1 (and_1_out, car_row[0], Dx);
  and and_2 (and_2_out, Sx, car_row[6]);
  or or_1 (or_1_out, and_1_out, and_2_out);
  // Probe on or_1_out
  and and_3 (SxOk, Sx, ~or_1_out);  // AND_Gate
  and and_4 (DxOk, ~or_1_out, Dx);  // AND_Gate

  assign car_row[4:1] = {4{car_row[5]}};
  // also tied to GND on the sheet: car_row[5]
endmodule

module gestore_schermo (
  input  [15:0] C1,
  input  [15:0] C2,
  input  [15:0] C3,
  input  [15:0] C4,
  input  [15:0] C5,
  input  [15:0] C6,
  input  [15:0] C7,
  input  Lose,
  input  Win,
  output [15:0] C1o,
  output [15:0] C2o,
  output [15:0] C3o,
  output [15:0] C4o,
  output [15:0] C5o,
  output [15:0] C6o,
  output [15:0] C7o
);

  wire [15:0] Lose_out_1, Lose_out_2, Lose_out_3, Lose_out_4, Lose_out_5, Lose_out_6, Lose_out_7, Win_out_1,
       Win_out_2, Win_out_3, Win_out_4, Win_out_5, Win_out_6, Win_out_7;

  // Probe on {Lose, Win}
  screen_fine u_Lose (
    .out_1(Lose_out_1), .out_2(Lose_out_2), .out_3(Lose_out_3), .out_4(Lose_out_4), .out_5(Lose_out_5),
    .out_6(Lose_out_6), .out_7(Lose_out_7));
  screen_win u_Win (
    .out_1(Win_out_1), .out_2(Win_out_2), .out_3(Win_out_3), .out_4(Win_out_4), .out_5(Win_out_5),
    .out_6(Win_out_6), .out_7(Win_out_7));
  Multiplexer #(.select(2), .width(16), .enable("false")) multiplexer_1 (
    .in0(C1), .in1(Win_out_1), .in2(Lose_out_1), .out(C1o), .sel({Lose, Win}));  // open: in3
  Multiplexer #(.select(2), .width(16), .enable("false")) multiplexer_2 (
    .in0(C2), .in1(Win_out_2), .in2(Lose_out_2), .out(C2o), .sel({Lose, Win}));  // open: in3
  Multiplexer #(.select(2), .width(16), .enable("false")) multiplexer_3 (
    .in0(C3), .in1(Win_out_3), .in2(Lose_out_3), .out(C3o), .sel({Lose, Win}));  // open: in3
  Multiplexer #(.select(2), .width(16), .enable("false")) multiplexer_4 (
    .in0(C4), .in1(Win_out_4), .in2(Lose_out_4), .out(C4o), .sel({Lose, Win}));  // open: in3
  Multiplexer #(.select(2), .width(16), .enable("false")) multiplexer_5 (
    .in0(C5), .in1(Win_out_5), .in2(Lose_out_5), .out(C5o), .sel({Lose, Win}));  // open: in3
  Multiplexer #(.select(2), .width(16), .enable("false")) multiplexer_6 (
    .in0(C6), .in1(Win_out_6), .in2(Lose_out_6), .out(C6o), .sel({Lose, Win}));  // open: in3
  Multiplexer #(.select(2), .width(16), .enable("false")) multiplexer_7 (
    .in0(C7), .in1(Win_out_7), .in2(Lose_out_7), .out(C7o), .sel({Lose, Win}));  // open: in3
endmodule

module _1_30_min_win_module (
  input  [3:0] seclow,
  input  [3:0] sechigh,
  input  [3:0] minutes,
  output Win
);

  and and_1 (Win, ~seclow[3], ~seclow[2], ~seclow[1], ~seclow[0], ~sechigh[3], ~sechigh[2], sechigh[1], sechigh[0], ~minutes[3], ~minutes[2], ~minutes[1], minutes[0]);  // AND_Gate
endmodule

module timer_with_reset (
  input  Reset,
  input  CLK,
  output [3:0] MinHigh,
  output [3:0] MinLow,
  output [3:0] SecHigh,
  output [3:0] SecLow,
  output Win
);

  wire and_1_out, and_2_out, and_3_out, and_4_out, counter_1_carry, counter_2_carry, d_ff_1_q, d_ff_2_q,
       d_ff_3_q, W;

  D_Flip_Flop d_ff_1 (.clk(CLK), .D(and_1_out), .Q(d_ff_1_q), .reset(Reset));  // open: Qn, preset, en
  and and_1 (and_1_out, and_2_out, and_3_out);
  and and_2 (and_2_out, MinLow[0], ~MinLow[1], ~MinLow[2], MinLow[3]);  // AND_Gate
  D_Flip_Flop d_ff_2 (.clk(CLK), .D(and_3_out), .Q(d_ff_2_q), .reset(Reset));  // open: Qn, preset, en
  and and_3 (and_3_out, SecHigh[0], ~SecHigh[1], SecHigh[2], ~SecHigh[3], ~SecLow[2], ~SecLow[2], SecLow[3], SecLow[0]);  // AND_Gate
  Counter #(.width(4), .max('h9)) counter_1 (
    .Q(MinLow), .carry(counter_1_carry), .clk(d_ff_2_q), .clr(Reset));  // open: load, D, count
  Counter #(.width(4), .max('h5)) counter_2 (
    .Q(MinHigh), .carry(counter_2_carry), .clk(d_ff_1_q), .clr(Reset));  // open: load, D, count
  // Probe on MinLow
  // Probe on SecHigh
  Counter #(.width(4), .max('h5)) counter_3 (.Q(SecHigh), .clk(d_ff_3_q), .clr(Reset));  // open: load, D, count, carry
  Counter #(.width(4), .max('h9)) counter_4 (.Q(SecLow), .clk(CLK), .clr(Reset));  // open: load, D, count, carry
  _1_30_min_win_module u_1_30_min_win_module_1 (.seclow(SecLow), .sechigh(SecHigh), .minutes(MinLow), .Win(W));
  and and_4 (and_4_out, SecLow[3], ~SecLow[2], ~SecLow[1], SecLow[0]);  // AND_Gate
  D_Flip_Flop d_ff_3 (.clk(CLK), .D(and_4_out), .Q(d_ff_3_q), .reset(Reset));  // open: Qn, preset, en
  // Probe on SecLow
  or or_1 (Win, counter_2_carry, W);
endmodule

module lose_check (
  input  [6:0] Last_Row,
  input  [6:0] Car_row,
  output Lose
);

  wire and_1_out, and_2_out, and_3_out, and_4_out, and_5_out, and_6_out, and_7_out;

  and and_1 (and_1_out, Car_row[0], Last_Row[0]);
  and and_2 (and_2_out, Car_row[1], Last_Row[1]);
  and and_3 (and_3_out, Car_row[2], Last_Row[2]);
  and and_4 (and_4_out, Car_row[3], Last_Row[3]);
  and and_5 (and_5_out, Car_row[4], Last_Row[4]);
  and and_6 (and_6_out, Car_row[5], Last_Row[5]);
  and and_7 (and_7_out, Car_row[6], Last_Row[6]);
  or or_1 (Lose, and_1_out, and_2_out, and_3_out, and_4_out, and_5_out, and_6_out, and_7_out);
endmodule

module screen_win (
  output [15:0] out_1,
  output [15:0] out_2,
  output [15:0] out_3,
  output [15:0] out_4,
  output [15:0] out_5,
  output [15:0] out_6,
  output [15:0] out_7
);

  DotMatrix #(.matrixcols(7), .matrixrows(16)) dotmatrix_1 (
    .col0(16'h800), .col1(16'h1c0c), .col2(16'h3e0c), .col3(16'h3ffc), .col4(16'hc), .col5(16'hc),
    .col6({16{1'b0}}));

  assign out_1 = 16'h800;
  assign out_2 = 16'h1c0c;
  assign out_3 = 16'h3e0c;
  assign out_4 = 16'h3ffc;
  assign out_5 = 16'hc;
  assign out_6 = 16'hc;
  assign out_7 = {16{1'b0}};
endmodule

module screen_fine (
  output [15:0] out_1,
  output [15:0] out_2,
  output [15:0] out_3,
  output [15:0] out_4,
  output [15:0] out_5,
  output [15:0] out_6,
  output [15:0] out_7
);

  DotMatrix #(.matrixcols(7), .matrixrows(16)) dotmatrix_1 (
    .col0(16'h7cf8), .col1(16'h5060), .col2(16'h5078), .col3({16{1'b0}}), .col4(16'h7cf8), .col5(16'ha8),
    .col6({16{1'b0}}));

  assign out_1 = 16'h7cf8;
  assign out_2 = 16'h5060;
  assign out_3 = 16'h5078;
  assign out_4 = {16{1'b0}};
  assign out_5 = 16'h7cf8;
  assign out_6 = 16'ha8;
  assign out_7 = {16{1'b0}};
endmodule

module _1_to_3_row_conv (
  input  [6:0] in_1,
  output [2:0] c1,
  output [2:0] c2,
  output [2:0] c3,
  output [2:0] c4,
  output [2:0] c5,
  output [2:0] c6,
  output [2:0] c7
);


  assign c1 = {in_1[0], 2'b00};
  assign c2 = {in_1[1], 2'b00};
  assign c3 = {in_1[2], 2'b00};
  assign c4 = {in_1[3], 2'b00};
  assign c5 = {in_1[4], 2'b00};
  assign c6 = {in_1[5], 2'b00};
  assign c7 = {in_1[6], 2'b00};
endmodule

module LR_controller (
  input  [6:0] LR,
  input  Win,
  output [6:0] D
);

  wire [6:0] and_1_out, and_2_out;

  assign and_1_out = LR & ~{7{Win}};  // AND_Gate and_1, 7 bits wide
  assign and_2_out = {7{1'b0}} & {7{Win}};  // AND_Gate and_2, 7 bits wide
  assign D = and_1_out | and_2_out;  // OR_Gate or_1, 7 bits wide
endmodule
